# Fritzing sketch Trilobot_scheme (saved by Fritzing 0.8.7b)
breadboards: 1

parts:
  Součástka1 = Arduino Mega 2560 (Rev3)
  Součástka2 = Sabertooth
  M1 = Stepper Motor - Unipolar  # not connected
  M2 = Stepper Motor - Unipolar  # not connected
  U1 = LCD-16X2 [package=lcd-16x2_noholes]
  LCM1602_IIC1 = LCM1602 IIC [part_number="LCM1602 IIC" chip_label="LCM1602 IIC" package="DIP (Dual Inline) [THT]"]
  SP1 = SPEAKER [package=pcb_mount_speaker]
  X1 = Sonar
  J1 = Infrared Proximity Sensor
  Součástka3 = SRF05 Ultrasonic Rangefinder
  LED1 = LED - 5mm [color="Blue (505nm)" package="5 mm [THT]"]

nets:
  N1: Součástka1.D21/SCL, LCM1602_IIC1.SCL, X1.SCL
  N2: Součástka1.D20/SDA, LCM1602_IIC1.SDA, X1.SDA
  N3: Součástka1.D19/RX1, Součástka2.S1
  N4: Součástka1.D13_PWM, LED1.anode
  VCC: Součástka1.5V, LCM1602_IIC1.VCC, X1.+5, J1.Vout, J1.Vcc, Součástka3.VCC
  GND: Součástka1.GND, Součástka2.B-, LCM1602_IIC1.GND, X1.GND, J1.GND, Součástka3.GND, LED1.cathode
  N5: Součástka1.VIN, Součástka2.B+
  N6: Součástka1.D5_PWM, SP1.-
  N7: Součástka1.D24, Součástka3.Trig
  N8: Součástka1.D26, Součástka3.Echo
  VSS: U1.VSS, LCM1602_IIC1.VSS
  VDD: U1.VDD, LCM1602_IIC1.VDD
  N9: U1.VO, LCM1602_IIC1.V0
  N10: U1.RS, LCM1602_IIC1.RS
  N11: U1.R_W, LCM1602_IIC1.RW
  N12: U1.E, LCM1602_IIC1.E
  N13: U1.DB0, LCM1602_IIC1.D0
  N14: U1.DB1, LCM1602_IIC1.D1
  N15: U1.DB2, LCM1602_IIC1.D2
  N16: U1.DB3, LCM1602_IIC1.D3
  N17: U1.DB4, LCM1602_IIC1.D4
  N18: U1.DB5, LCM1602_IIC1.D5
  N19: U1.DB6, LCM1602_IIC1.D6
  N20: U1.DB7, LCM1602_IIC1.D7
  N21: U1.A, LCM1602_IIC1.A
  N22: U1.K, LCM1602_IIC1.K
  N23: LCM1602_IIC1.LED_A, LCM1602_IIC1.LED_B

notes:
  6-12 V Power supply

custom parts:
  Stepper Motor - Unipolar: A basic unipolar stepper motor
  LCM1602 IIC: I2C-Module to use a 1602 or 2004 LCD on with the wire.h libory Serial LCD Modul
  Sonar: Devantech SRF08 sonar range-finder. I2C interface. Other Devantech sonars similar
